// Logisim project Q1.circ as structural Verilog
module _4bit_mod2_div (
  input  [3:0] dividend,
  input  [3:0] divisor,
  output [2:0] \_3位余数 ,
  output \_1位商 
);

  wire [3:0] multiplexer_1_out, xor_1_out;

  assign xor_1_out = dividend ^ divisor;  // XOR_Gate xor_1, 4 bits wide
  BitSelector #(.width(4)) bitselector_1 (.in(dividend), .out(\_1位商 ), .sel(2'b11));
  // Probe on \_1位商 
  // Probe on multiplexer_1_out
  Multiplexer #(.width(4)) multiplexer_1 (
    .in0(dividend), .in1(xor_1_out), .out(multiplexer_1_out), .sel(\_1位商 ));  // open: en
  BitSelector #(.width(4), .group(3)) bitselector_2 (.in(multiplexer_1_out), .out(\_3位余数 ), .sel(1'b0));
endmodule

module CRC (
  input  [7:0] input_dividend,
  input  [3:0] divisor,
  output [10:0] out_3
);

  wire _0_bit, _1_bit, _2_bit, _3_bit;
  wire [2:0] \_1__3位余数 , \n4bit_mod2_div_1__3位余数 , \n4bit_mod2_div_2__3位余数 , \n4bit_mod2_div_3__3位余数 ,
       \n4bit_mod2_div_4__3位余数 , \n4bit_mod2_div_5__3位余数 , \n4bit_mod2_div_6__3位余数 ;
  wire [10:0] bitselector_1_out, mod_2_number;

  BitSelector #(.group(11)) bitselector_1 (.in(input_dividend), .out(bitselector_1_out), .sel(1'b0));
  // Probe on mod_2_number[10:7]
  // Probe on bitselector_1_out
  // Probe on \_1__3位余数 
  _4bit_mod2_div _1 (.dividend(mod_2_number[10:7]), .divisor(divisor), .\_3位余数 (\_1__3位余数 ));  // open: _1位商
  // Probe on mod_2_number
  Shifter #(.width(11)) shifter_1 (.in(bitselector_1_out), .\dist (4'b0011), .out(mod_2_number));
  // Probe on {\_1__3位余数 , _3_bit}
  // Probe on \n4bit_mod2_div_1__3位余数 
  _4bit_mod2_div u_4bit_mod2_div_1 (
    .dividend({\_1__3位余数 , _3_bit}), .divisor(divisor), .\_3位余数 (\n4bit_mod2_div_1__3位余数 ));  // open: _1位商
  BitSelector #(.width(11)) bitselector_2 (.in(mod_2_number), .out(_3_bit), .sel(4'b0110));
  BitSelector #(.width(11)) bitselector_3 (.in(mod_2_number), .out(_2_bit), .sel(4'b0101));
  BitSelector #(.width(11)) bitselector_4 (.in(mod_2_number), .out(_1_bit), .sel(4'b0100));
  BitSelector #(.width(11)) bitselector_5 (.in(mod_2_number), .out(_0_bit), .sel(4'b0011));
  // Probe on {\n4bit_mod2_div_1__3位余数 , _2_bit}
  // Probe on \n4bit_mod2_div_2__3位余数 
  _4bit_mod2_div u_4bit_mod2_div_2 (
    .dividend({\n4bit_mod2_div_1__3位余数 , _2_bit}), .divisor(divisor), .\_3位余数 (\n4bit_mod2_div_2__3位余数 ));  // open: _1位商
  // Probe on {\n4bit_mod2_div_2__3位余数 , _1_bit}
  // Probe on \n4bit_mod2_div_3__3位余数 
  _4bit_mod2_div u_4bit_mod2_div_3 (
    .dividend({\n4bit_mod2_div_2__3位余数 , _1_bit}), .divisor(divisor), .\_3位余数 (\n4bit_mod2_div_3__3位余数 ));  // open: _1位商
  // Probe on \n4bit_mod2_div_4__3位余数 
  _4bit_mod2_div u_4bit_mod2_div_4 (
    .dividend({\n4bit_mod2_div_3__3位余数 , _0_bit}), .divisor(divisor), .\_3位余数 (\n4bit_mod2_div_4__3位余数 ));  // open: _1位商
  // Probe on {\n4bit_mod2_div_4__3位余数 , 1'b0}
  _4bit_mod2_div u_4bit_mod2_div_5 (
    .dividend({\n4bit_mod2_div_4__3位余数 , 1'b0}), .divisor(divisor), .\_3位余数 (\n4bit_mod2_div_5__3位余数 ));  // open: _1位商
  // Probe on \n4bit_mod2_div_5__3位余数 
  // Probe on {\n4bit_mod2_div_5__3位余数 , 1'b0}
  // Probe on \n4bit_mod2_div_6__3位余数 
  _4bit_mod2_div u_4bit_mod2_div_6 (
    .dividend({\n4bit_mod2_div_5__3位余数 , 1'b0}), .divisor(divisor), .\_3位余数 (\n4bit_mod2_div_6__3位余数 ));  // open: _1位商
  // Probe on {\n4bit_mod2_div_6__3位余数 , 1'b0}
  // Probe on out_3[2:0]
  _4bit_mod2_div u_4bit_mod2_div_7 (
    .dividend({\n4bit_mod2_div_6__3位余数 , 1'b0}), .divisor(divisor), .\_3位余数 (out_3[2:0]));  // open: _1位商

  assign out_3[10:3] = input_dividend;

  // Other names for the same wires on the sheet: remainder[2:0] = out_3[2:0]
endmodule
