// Logisim project Q3.circ as structural Verilog: 4 circuits, main circuit main
module main (
  input  [1:0] dir,
  input  reset,
  output arrive,
  output hit
);

  wire clock_1_out;
  wire [3:0] register_1_q, \状态转移_1_s0 ;

  \状态转移  \u_状态转移_1  (
    .C3(register_1_q[3]), .C2(register_1_q[2]), .C1(register_1_q[1]), .C0(register_1_q[0]), .B1(dir[1]),
    .B0(dir[0]), .S3(\状态转移_1_s0 [3]), .S2(\状态转移_1_s0 [2]), .S1(\状态转移_1_s0 [1]), .S0(\状态转移_1_s0 [0]));
  Register #(.width(4)) register_1 (.D(\状态转移_1_s0 ), .Q(register_1_q), .clk(clock_1_out), .clr(reset));  // open: en
  Clock clock_1 (.out(clock_1_out));
  \状态输出  \u_状态输出_1  (
    .C3(register_1_q[3]), .C2(register_1_q[2]), .C1(register_1_q[1]), .C0(register_1_q[0]), .arrive(arrive),
    .hit(hit));
endmodule

module \状态转移  (
  input  C3,
  input  C2,
  input  C1,
  input  C0,
  input  B1,
  input  B0,
  output S3,
  output S2,
  output S1,
  output S0
);

  wire and_1_out, and_2_out, and_3_out, and_4_out, and_5_out, and_6_out, and_7_out, and_8_out, and_9_out,
       and_10_out, and_11_out, and_12_out, and_13_out, and_14_out, and_15_out, and_16_out, and_17_out,
       and_18_out, and_19_out, and_20_out, and_21_out, and_22_out, and_23_out, and_24_out, and_25_out,
       and_26_out, and_27_out, and_28_out, not_1_out, not_2_out, not_3_out, not_4_out, not_5_out, not_6_out,
       not_7_out, not_8_out, not_9_out, not_10_out, not_11_out, not_12_out, not_13_out, not_14_out,
       not_15_out, not_16_out, not_17_out, not_18_out, not_19_out, not_20_out, not_21_out, not_22_out,
       not_23_out, not_24_out, not_25_out, not_26_out, not_27_out, not_28_out, not_29_out, not_30_out,
       not_31_out, not_32_out, not_33_out, not_34_out, not_35_out, not_36_out, not_37_out, not_38_out,
       not_39_out, not_40_out, not_41_out, not_42_out, not_43_out, not_44_out, not_45_out, not_46_out,
       not_47_out, not_48_out, not_49_out, not_50_out, not_51_out, not_52_out, not_53_out, not_54_out,
       not_55_out, not_56_out, not_57_out, not_58_out, not_59_out, not_60_out, not_61_out, not_62_out,
       not_63_out, not_64_out, not_65_out, not_66_out, not_67_out, not_68_out, not_69_out, not_70_out,
       not_71_out, not_72_out, not_73_out, not_74_out, not_75_out, not_76_out, not_77_out, not_78_out,
       not_79_out, not_80_out, not_81_out, not_82_out;

  not not_1 (not_1_out, C3);
  not not_2 (not_2_out, C2);
  not not_3 (not_3_out, B1);
  not not_4 (not_4_out, C3);
  not not_5 (not_5_out, C2);
  not not_6 (not_6_out, B0);
  not not_7 (not_7_out, C2);
  not not_8 (not_8_out, C1);
  not not_9 (not_9_out, C0);
  not not_10 (not_10_out, B1);
  not not_11 (not_11_out, C2);
  not not_12 (not_12_out, C1);
  not not_13 (not_13_out, C0);
  not not_14 (not_14_out, B0);
  not not_15 (not_15_out, C3);
  not not_16 (not_16_out, C2);
  not not_17 (not_17_out, C0);
  not not_18 (not_18_out, C3);
  not not_19 (not_19_out, C2);
  not not_20 (not_20_out, C1);
  not not_21 (not_21_out, C0);
  not not_22 (not_22_out, C3);
  not not_23 (not_23_out, C2);
  not not_24 (not_24_out, C1);
  not not_25 (not_25_out, C3);
  not not_26 (not_26_out, C2);
  not not_27 (not_27_out, B1);
  not not_28 (not_28_out, B0);
  not not_29 (not_29_out, C3);
  not not_30 (not_30_out, C0);
  not not_31 (not_31_out, C3);
  not not_32 (not_32_out, B1);
  not not_33 (not_33_out, B0);
  not not_34 (not_34_out, C3);
  not not_35 (not_35_out, C3);
  not not_36 (not_36_out, C1);
  not not_37 (not_37_out, C2);
  not not_38 (not_38_out, C1);
  not not_39 (not_39_out, C0);
  not not_40 (not_40_out, B1);
  not not_41 (not_41_out, B0);
  not not_42 (not_42_out, C3);
  not not_43 (not_43_out, C2);
  not not_44 (not_44_out, C1);
  not not_45 (not_45_out, B1);
  not not_46 (not_46_out, C3);
  not not_47 (not_47_out, C2);
  not not_48 (not_48_out, C1);
  not not_49 (not_49_out, C3);
  not not_50 (not_50_out, C0);
  not not_51 (not_51_out, B1);
  not not_52 (not_52_out, B0);
  not not_53 (not_53_out, C3);
  not not_54 (not_54_out, C0);
  not not_55 (not_55_out, C3);
  not not_56 (not_56_out, C0);
  not not_57 (not_57_out, B1);
  not not_58 (not_58_out, C3);
  not not_59 (not_59_out, B1);
  not not_60 (not_60_out, B0);
  not not_61 (not_61_out, C3);
  not not_62 (not_62_out, C3);
  not not_63 (not_63_out, C2);
  not not_64 (not_64_out, C0);
  not not_65 (not_65_out, B0);
  not not_66 (not_66_out, C3);
  not not_67 (not_67_out, C2);
  not not_68 (not_68_out, C1);
  not not_69 (not_69_out, B1);
  not not_70 (not_70_out, C2);
  not not_71 (not_71_out, C1);
  not not_72 (not_72_out, C0);
  not not_73 (not_73_out, C3);
  not not_74 (not_74_out, C2);
  not not_75 (not_75_out, C3);
  not not_76 (not_76_out, C1);
  not not_77 (not_77_out, C3);
  not not_78 (not_78_out, B0);
  not not_79 (not_79_out, C3);
  not not_80 (not_80_out, C3);
  not not_81 (not_81_out, C0);
  not not_82 (not_82_out, B1);
  and and_1 (and_1_out, not_1_out, not_2_out, C1, C0, not_3_out, B0);
  and and_2 (and_2_out, not_4_out, not_5_out, C1, C0, B1, not_6_out);
  and and_3 (and_3_out, C3, not_7_out, not_8_out, not_9_out, not_10_out, B0);
  and and_4 (and_4_out, C3, not_11_out, not_12_out, not_13_out, B1, not_14_out);
  and and_5 (and_5_out, not_15_out, not_16_out, not_17_out, B0);
  and and_6 (and_6_out, not_18_out, not_19_out, not_20_out, not_21_out, B1);
  and and_7 (and_7_out, not_22_out, not_23_out, not_24_out, B1, B0);
  and and_8 (and_8_out, not_25_out, not_26_out, C1, not_27_out, not_28_out);
  and and_9 (and_9_out, not_29_out, C1, not_30_out, B1, B0);
  and and_10 (and_10_out, not_31_out, C1, C0, not_32_out, not_33_out);
  and and_11 (and_11_out, not_34_out, C2, C0, B0);
  and and_12 (and_12_out, not_35_out, C2, not_36_out, C0, B1);
  and and_13 (and_13_out, C3, not_37_out, not_38_out, not_39_out, not_40_out, not_41_out);
  and and_14 (and_14_out, not_42_out, not_43_out, not_44_out, C0, not_45_out);
  and and_15 (and_15_out, not_46_out, not_47_out, not_48_out, C0, B0);
  and and_16 (and_16_out, not_49_out, C1, not_50_out, not_51_out, not_52_out);
  and and_17 (and_17_out, not_53_out, C1, not_54_out, B1, B0);
  and and_18 (and_18_out, not_55_out, C2, C1, not_56_out, not_57_out);
  and and_19 (and_19_out, not_58_out, C2, C1, not_59_out, not_60_out);
  and and_20 (and_20_out, not_61_out, C2, C1, B1, B0);
  and and_21 (and_21_out, not_62_out, not_63_out, not_64_out, not_65_out);
  and and_22 (and_22_out, not_66_out, not_67_out, not_68_out, not_69_out, B0);
  and and_23 (and_23_out, not_70_out, not_71_out, not_72_out, B1, B0);
  and and_24 (and_24_out, not_73_out, not_74_out, C1, B1, B0);
  and and_25 (and_25_out, not_75_out, C2, not_76_out, C0);
  and and_26 (and_26_out, not_77_out, C2, C0, not_78_out);
  and and_27 (and_27_out, not_79_out, C2, C0, B1);
  and and_28 (and_28_out, not_80_out, C2, C1, not_81_out, not_82_out, B0);
  or or_1 (S3, and_1_out, and_2_out, and_3_out, and_4_out);
  or or_2 (S2, and_5_out, and_6_out, and_7_out, and_8_out, and_9_out, and_10_out, and_11_out, and_12_out, and_13_out);
  or or_3 (S1, and_14_out, and_15_out, and_16_out, and_17_out, and_18_out, and_19_out, and_20_out);
  or or_4 (S0, and_21_out, and_22_out, and_23_out, and_24_out, and_25_out, and_26_out, and_27_out, and_28_out);
endmodule

module \状态输出  (
  input  C3,
  input  C2,
  input  C1,
  input  C0,
  output arrive,
  output hit
);

  wire and_2_out, and_3_out, and_4_out, not_1_out, not_2_out, not_3_out, not_4_out, not_5_out, not_6_out,
       not_7_out, not_8_out;

  not not_1 (not_1_out, C3);
  not not_2 (not_2_out, C1);
  not not_3 (not_3_out, C0);
  not not_4 (not_4_out, C3);
  not not_5 (not_5_out, C3);
  not not_6 (not_6_out, C2);
  not not_7 (not_7_out, C1);
  not not_8 (not_8_out, C0);
  and and_1 (arrive, not_1_out, C2, not_2_out, not_3_out);
  and and_2 (and_2_out, not_4_out, C2, C0);
  and and_3 (and_3_out, not_5_out, C2, C1);
  or or_1 (hit, and_2_out, and_3_out, and_4_out);
  and and_4 (and_4_out, C3, not_6_out, not_7_out, not_8_out);
endmodule

module navigation (
  input  [1:0] dir,
  input  clk,
  input  reset,
  output arrive,
  output hit
);

  wire clock_1_out;
  wire [3:0] register_1_q, \状态转移_1_s0 ;

  \状态转移  \u_状态转移_1  (
    .C3(register_1_q[3]), .C2(register_1_q[2]), .C1(register_1_q[1]), .C0(register_1_q[0]), .B1(dir[1]),
    .B0(dir[0]), .S3(\状态转移_1_s0 [3]), .S2(\状态转移_1_s0 [2]), .S1(\状态转移_1_s0 [1]), .S0(\状态转移_1_s0 [0]));
  Register #(.width(4)) register_1 (.D(\状态转移_1_s0 ), .Q(register_1_q), .clk(clock_1_out), .clr(reset));  // open: en
  Clock clock_1 (.out(clock_1_out));
  \状态输出  \u_状态输出_1  (
    .C3(register_1_q[3]), .C2(register_1_q[2]), .C1(register_1_q[1]), .C0(register_1_q[0]), .arrive(arrive),
    .hit(hit));
endmodule
