// Logisim project Q4.circ as structural Verilog
module \状态转移和输出  (
  input  C1,
  input  C0,
  input  In1,
  input  In0,
  output S1,
  output S0,
  output Z
);

  wire and_1_out, and_2_out, and_3_out, and_5_out, and_6_out, and_7_out, not_1_out, not_2_out, not_3_out,
       not_4_out, not_5_out, not_6_out, not_7_out, not_8_out, not_9_out, not_10_out, not_11_out, not_12_out,
       not_13_out, not_14_out;

  not not_1 (not_1_out, C1);
  and and_1 (and_1_out, not_1_out, C0, not_2_out);
  not not_2 (not_2_out, In1);
  not not_3 (not_3_out, C1);
  and and_2 (and_2_out, not_3_out, C0, not_4_out);
  not not_4 (not_4_out, In0);
  and and_3 (and_3_out, C1, not_5_out, not_6_out);
  not not_5 (not_5_out, C0);
  not not_6 (not_6_out, In0);
  not not_7 (not_7_out, C1);
  not not_8 (not_8_out, C0);
  not not_9 (not_9_out, In1);
  not not_10 (not_10_out, C1);
  not not_11 (not_11_out, In0);
  not not_12 (not_12_out, C0);
  not not_13 (not_13_out, In0);
  and and_4 (Z, C1, C0, not_14_out);
  not not_14 (not_14_out, In0);
  or or_1 (S1, and_1_out, and_2_out, and_3_out);
  and and_5 (and_5_out, not_7_out, not_8_out, not_9_out, In0);
  and and_6 (and_6_out, not_10_out, C0, not_11_out);
  or or_2 (S0, and_5_out, and_6_out, and_7_out);
  and and_7 (and_7_out, C1, not_12_out, not_13_out);
endmodule

module \状态转移  (
  input  C1,
  input  C0,
  input  In1,
  input  In0,
  output S1,
  output S0
);

  wire and_1_out, and_2_out, and_3_out, and_4_out, and_5_out, and_6_out, not_1_out, not_2_out, not_3_out,
       not_4_out, not_5_out, not_6_out, not_7_out, not_8_out, not_9_out, not_10_out, not_11_out, not_12_out,
       not_13_out;

  not not_1 (not_1_out, C1);
  and and_1 (and_1_out, not_1_out, C0, not_2_out);
  not not_2 (not_2_out, In1);
  not not_3 (not_3_out, C1);
  and and_2 (and_2_out, not_3_out, C0, not_4_out);
  not not_4 (not_4_out, In0);
  and and_3 (and_3_out, C1, not_5_out, not_6_out);
  not not_5 (not_5_out, C0);
  not not_6 (not_6_out, In0);
  not not_7 (not_7_out, C1);
  not not_8 (not_8_out, C0);
  not not_9 (not_9_out, In1);
  not not_10 (not_10_out, C1);
  not not_11 (not_11_out, In0);
  not not_12 (not_12_out, C0);
  not not_13 (not_13_out, In0);
  or or_1 (S1, and_1_out, and_2_out, and_3_out);
  and and_4 (and_4_out, not_7_out, not_8_out, not_9_out, In0);
  and and_5 (and_5_out, not_10_out, C0, not_11_out);
  or or_2 (S0, and_4_out, and_5_out, and_6_out);
  and and_6 (and_6_out, C1, not_12_out, not_13_out);
endmodule

module \状态输出  (
  input  C1,
  input  C0,
  input  In1,
  input  In0,
  output Z
);

  wire not_1_out;

  and and_1 (Z, C1, C0, not_1_out);
  not not_1 (not_1_out, In0);
endmodule

module fsm (
  input  CLR,
  input  [1:0] In,
  output Z
);

  wire and_1_out, clock_1_out, register_1_q;
  wire [1:0] register_2_q, \状态转移_1_s0 ;

  Clock clock_1 (.out(clock_1_out));
  \状态转移  \u_状态转移_1  (
    .C1(register_2_q[1]), .C0(register_2_q[0]), .In1(In[1]), .In0(In[0]), .S1(\状态转移_1_s0 [1]),
    .S0(\状态转移_1_s0 [0]));
  Register #(.width(1)) register_1 (.D(CLR), .Q(register_1_q), .clk(clock_1_out));  // open: en, clr
  Register #(.width(2)) register_2 (.D(\状态转移_1_s0 ), .Q(register_2_q), .clk(clock_1_out), .clr(and_1_out));  // open: en
  and and_1 (and_1_out, CLR, register_1_q);
  \状态输出  \u_状态输出_1  (.C1(register_2_q[1]), .C0(register_2_q[0]), .In1(In[1]), .In0(In[0]), .Z(Z));
endmodule
