// Logisim project float_to_int.circ as structural Verilog
module test (
  input  [15:0] float,
  output [31:0] out_2
);

  wire comparator_1_lt, sign;
  wire [4:0] adder_1_out, exponent, not_1_out, subtractor_1_out;
  wire [9:0] fraction, shifter_1_out;
  wire [14:0] bitselector_4_out;
  wire [21:0] shifter_1_out_2;
  wire [31:0] bit_extender_1_out;

  // Probe on sign
  BitSelector #(.width(16)) bitselector_1 (.in(float), .out(sign), .sel(4'b1111));
  // Probe on exponent
  BitSelector #(.width(16), .group(5)) bitselector_2 (.in(float), .out(exponent), .sel(2'b10));
  BitSelector #(.width(16), .group(10)) bitselector_3 (.in(float), .out(fraction), .sel(1'b0));
  // Probe on fraction
  BitSelector #(.width(16), .group(15)) bitselector_4 (.in(float), .out(bitselector_4_out), .sel(1'b0));
  Subtractor #(.width(5)) subtractor_1 (.a(exponent), .b(5'b01111), .out(subtractor_1_out));  // open: bin, bout
  // Probe on subtractor_1_out
  assign not_1_out = ~subtractor_1_out;  // NOT_Gate not_1, 5 bits wide
  assign bit_extender_1_out = {{22{1'b0}}, fraction};  // Bit_Extender bit_extender_1
  Comparator #(.width(5)) comparator_1 (.a(subtractor_1_out), .b({5{1'b0}}), .lt(comparator_1_lt));  // open: gt, eq
  // Probe on adder_1_out
  Adder #(.width(5)) adder_1 (.a(not_1_out), .b(5'b00001), .out(adder_1_out));  // open: cin, cout
  // Probe on bit_extender_1_out
  Shifter #(.width(32), .shift("ar")) shifter_1 (
    .in(bit_extender_1_out), .\dist (adder_1_out), .out({shifter_1_out_2, shifter_1_out}));
  // Probe on {shifter_1_out_2, shifter_1_out}
  // Probe on adder_1_out
  // Probe on {shifter_1_out_2, shifter_1_out}
  // Probe on shifter_1_out_2
  assign out_2 = {{10{shifter_1_out_2[21]}}, shifter_1_out_2};  // Bit_Extender bit_extender_2
  // Probe on out_2

  // Other names for the same wires on the sheet: out_positive[31:0] = out_2
endmodule

module ftoi (
  input  [15:0] float,
  output [31:0] \int 
);

  wire comparator_1_eq, comparator_1_gt, comparator_2_eq, or_1_out, sign;
  wire [4:0] E, exponent;
  wire [5:0] subtractor_1_out;
  wire [9:0] fraction;
  wire [31:0] adder_1_out, bit_extender_1_out, bit_extender_3_out, multiplexer_1_out, multiplexer_2_out,
       not_1_out, shifter_1_out;

  // Probe on bit_extender_1_out
  assign bit_extender_1_out = {{21{1'b0}}, {1'b1, fraction}};  // Bit_Extender bit_extender_1
  // Probe on shifter_1_out
  Shifter #(.width(32)) shifter_1 (.in(bit_extender_1_out), .\dist (E), .out(shifter_1_out));
  Subtractor #(.width(6)) subtractor_1 (
    .a({1'b0, exponent}), .b(6'b001111), .out(subtractor_1_out));  // open: bin, bout
  Bit_Extender #(.in_width(6), .out_width(5)) bit_extender_2 (.in(subtractor_1_out), .out(E));
  // Probe on E
  assign not_1_out = ~bit_extender_3_out;  // NOT_Gate not_1, 32 bits wide
  // Probe on bit_extender_3_out
  assign bit_extender_3_out = {{10{1'b0}}, shifter_1_out[31:10]};  // Bit_Extender bit_extender_3
  Adder #(.width(32)) adder_1 (.a(not_1_out), .b(32'h1), .out(adder_1_out));  // open: cin, cout
  Multiplexer #(.width(32)) multiplexer_1 (
    .in0(bit_extender_3_out), .in1(adder_1_out), .out(multiplexer_1_out), .sel(sign));  // open: en
  Comparator #(.width(6)) comparator_1 (
    .a(subtractor_1_out), .b({6{1'b0}}), .gt(comparator_1_gt), .eq(comparator_1_eq));  // open: lt
  // Probe on multiplexer_1_out
  Multiplexer #(.width(32)) multiplexer_2 (
    .in0({32{1'b0}}), .in1(multiplexer_1_out), .out(multiplexer_2_out), .sel(or_1_out));  // open: en
  or or_1 (or_1_out, comparator_1_gt, comparator_1_eq);
  Comparator #(.width(5)) comparator_2 (.a(exponent), .b({5{1'b1}}), .eq(comparator_2_eq));  // open: gt, lt
  Multiplexer #(.width(32)) multiplexer_3 (
    .in0(multiplexer_2_out), .in1({32{1'b0}}), .out(\int ), .sel(comparator_2_eq));  // open: en
  // Probe on sign
  BitSelector #(.width(16)) bitselector_1 (.in(float), .out(sign), .sel(4'b1111));
  // Probe on exponent
  BitSelector #(.width(16), .group(5)) bitselector_2 (.in(float), .out(exponent), .sel(2'b10));
  BitSelector #(.width(16), .group(10)) bitselector_3 (.in(float), .out(fraction), .sel(1'b0));
  // Probe on fraction
endmodule
