// Logisim project CPU_apperance_grf.circ as structural Verilog: 13 circuits, main circuit main
module main (
  input  Reset,
  output [31:0] out_2,
  output out_3,
  output [4:0] out_4,
  output [31:0] out_5,
  output out_6,
  output [4:0] out_7,
  output [31:0] out_8
);

  wire alu_1_zero, Clk, ctrl_1_npcop, ctrl_1_re, EXTOp, M1_Sel, M3_Sel;
  wire [1:0] M2_Sel;
  wire [2:0] ctrl_1_aluctrl__2_0;
  wire [4:0] spl_1_rs____25_21, spl_1_rt____20_16;
  wire [5:0] funct____5_0, spl_1_opcode____31_26;
  wire [15:6] Imm__15_0;
  wire [31:0] ALU_Result, DM_RD, ext_1_ext32__31_0, grf_1_rd1, multiplexer_3_out, shifter_1_out;

  Clock clock_1 (.out(Clk));
  IFU ifu_1 (
    .Clk(Clk), .Reset(Reset), .Zero(alu_1_zero), .Branch(ctrl_1_npcop),
    .Imm__15_0({Imm__15_0, funct____5_0}), .Instr__31_0(out_2));
  SPL spl_1 (
    .Instr(out_2), .opcode____31_26(spl_1_opcode____31_26), .rs____25_21(spl_1_rs____25_21),
    .rt____20_16(spl_1_rt____20_16), .rd____15_11(Imm__15_0[15:11]), .shamt____10_6(Imm__15_0[10:6]),
    .funct____5_0(funct____5_0));
  EXT ext_1 (.imm16__15_0({Imm__15_0, funct____5_0}), .ExtOp(EXTOp), .ext32__31_0(ext_1_ext32__31_0));
  Shifter #(.width(32)) shifter_1 (.in(ext_1_ext32__31_0), .\dist (5'b10000), .out(shifter_1_out));
  Ctrl ctrl_1 (
    .opcode__5_0(spl_1_opcode____31_26), .func__5_0(funct____5_0), .NPCOp(ctrl_1_npcop), .EXTOp(EXTOp),
    .RegWrite(out_3), .MemWrite(out_6), .M1_Sel(M1_Sel), .M3_Sel(M3_Sel), .M2_Sel(M2_Sel),
    .ALUCtrl__2_0(ctrl_1_aluctrl__2_0), .RE(ctrl_1_re));
  Multiplexer #(.width(5)) multiplexer_1 (
    .in0(Imm__15_0[15:11]), .in1(spl_1_rt____20_16), .out(out_4), .sel(M1_Sel));  // open: en
  Multiplexer #(.select(2), .width(32)) multiplexer_2 (
    .in0(ALU_Result), .in1(DM_RD), .in2(shifter_1_out), .out(out_5), .sel(M2_Sel));  // open: in3, en
  GRF grf_1 (
    .A1(spl_1_rs____25_21), .A2(spl_1_rt____20_16), .A3(out_4), .WD(out_5), .RD1(grf_1_rd1), .RD2(out_8),
    .clk(Clk), .reset(Reset), .WE(out_3));
  Multiplexer #(.width(32)) multiplexer_3 (
    .in0(out_8), .in1(ext_1_ext32__31_0), .out(multiplexer_3_out), .sel(M3_Sel));  // open: en
  ALU alu_1 (
    .ALUCtrl__2_0(ctrl_1_aluctrl__2_0), .A__31_0(grf_1_rd1), .B__31_0(multiplexer_3_out),
    .Result(ALU_Result), .Zero(alu_1_zero));
  get_address get_address_1 (.data(ALU_Result), .address(out_7));
  DM dm_1 (.A__4_0(out_7), .WD__31_0(out_8), .RD__31_0(DM_RD), .WE(out_6), .Clk(Clk), .RE(ctrl_1_re), .Reset(Reset));
  // Probe on out_4
  // Probe on out_5
  // Probe on out_7
  // Probe on out_8
  // Probe on out_2

  // Other names for the same wires on the sheet: Imm__15_0[5:0] = funct____5_0; shamt____10_6[4:0] = Imm__15_0[10:6];
  //   rd____15_11[4:0] = Imm__15_0[15:11]; Instr[31:0] = out_2; MemAddr[4:0] = out_7; MemData[31:0] = out_8;
  //   MemWrite = out_6; RegAddr[4:0] = out_4; RegData[31:0] = out_5; RegWrite = out_3
endmodule

module IFU (
  input  Clk,
  input  Reset,
  input  Zero,
  input  Branch,
  input  [15:0] Imm__15_0,
  output [31:0] Instr__31_0
);

  wire [31:0] ifu_npc_1_npc, PC_q;

  Register #(.width(32)) PC (.D(ifu_npc_1_npc), .Q(PC_q), .clk(Clk), .clr(Reset));  // open: en
  IFU_NPC ifu_npc_1 (.PC__31_0(PC_q), .Imm__15_0(Imm__15_0), .Zero(Zero), .Branch(Branch), .NPC(ifu_npc_1_npc));
  IFU_IM ifu_im_1 (.A(PC_q[6:2]), .RD(Instr__31_0));
endmodule

module IFU_NPC (
  input  [31:0] PC__31_0,
  input  [15:0] Imm__15_0,
  input  Zero,
  input  Branch,
  output [31:0] NPC
);

  wire and_1_out;
  wire [31:0] adder_1_out, adder_2_out, bit_extender_1_out, shifter_1_out;

  assign bit_extender_1_out = {{16{Imm__15_0[15]}}, Imm__15_0};  // Bit_Extender bit_extender_1
  // Probe on bit_extender_1_out
  and and_1 (and_1_out, Zero, Branch);
  Adder #(.width(32)) adder_1 (.a(PC__31_0), .b(32'h4), .out(adder_1_out));  // open: cin, cout
  Shifter #(.width(32)) shifter_1 (.in(bit_extender_1_out), .\dist (5'b00010), .out(shifter_1_out));
  // Probe on shifter_1_out
  // Probe on adder_1_out
  Adder #(.width(32)) adder_2 (.a(adder_1_out), .b(shifter_1_out), .out(adder_2_out));  // open: cin, cout
  Multiplexer #(.width(32)) multiplexer_1 (
    .in0(adder_1_out), .in1(adder_2_out), .out(NPC), .sel(and_1_out));  // open: en
endmodule

module IFU_IM (
  input  [4:0] A,
  output [31:0] RD
);

  // Probe on A
  ROM #(.addrWidth(5), .dataWidth(32)) rom_1 (.addr(A), .data(RD));  // open: sel

  // Notes on the sheet:
  //   contents of rom_1 (hex, n*v repeats v):
  //   3404ffff 3c04ffff 802821 10800002 3406fadc 10850001 ac040000 ac060004
endmodule

module GRF (
  input  clk,
  input  reset,
  input  WE,
  input  [4:0] A1,
  input  [4:0] A2,
  input  [4:0] A3,
  input  [31:0] WD,
  output [31:0] RD1,
  output [31:0] RD2
);

  wire and_1_out, and_2_out, and_3_out, and_4_out, and_5_out, and_6_out, and_7_out, and_8_out, and_9_out,
       and_10_out, and_11_out, and_12_out, and_13_out, and_14_out, and_15_out, and_16_out, and_17_out,
       and_18_out, and_19_out, and_20_out, and_21_out, and_22_out, and_23_out, and_24_out, and_25_out,
       and_26_out, and_27_out, and_28_out, and_29_out, and_30_out, and_31_out, data__0, data__1, data__2,
       data__3, data__4, data__5, data__6, data__7, data__8, data__9, data__10, data__11, data__12, data__13,
       data__14, data__15, data__16, data__17, data__18, data__19, data__20, data__21, data__22, data__23,
       data__24, data__25, data__26, data__27, data__28, data__29, data__30, data__31;
  wire [31:0] out__0, out__1, out__2, out__3, out__4, out__5, out__6, out__7, out__8, out__9, out__10,
       out__11, out__12, out__13, out__14, out__15, out__16, out__17, out__18, out__19, out__20, out__21,
       out__22, out__23, out__24, out__25, out__26, out__27, out__28, out__29, out__30, out__31;

  and and_1 (and_1_out, WE, data__4);
  and and_2 (and_2_out, WE, data__8);
  and and_3 (and_3_out, WE, data__12);
  and and_4 (and_4_out, WE, data__16);
  and and_5 (and_5_out, WE, data__20);
  and and_6 (and_6_out, WE, data__24);
  and and_7 (and_7_out, WE, data__28);
  Decoder #(.select(5)) decoder_1 (
    .out0(data__0), .out1(data__1), .out2(data__2), .out3(data__3), .out4(data__4), .out5(data__5),
    .out6(data__6), .out7(data__7), .out8(data__8), .out9(data__9), .out10(data__10), .out11(data__11),
    .out12(data__12), .out13(data__13), .out14(data__14), .out15(data__15), .out16(data__16),
    .out17(data__17), .out18(data__18), .out19(data__19), .out20(data__20), .out21(data__21),
    .out22(data__22), .out23(data__23), .out24(data__24), .out25(data__25), .out26(data__26),
    .out27(data__27), .out28(data__28), .out29(data__29), .out30(data__30), .out31(data__31), .sel(A3));  // open: en
  Register #(.width(32)) _0 (.D({32{1'b0}}), .Q(out__0), .clk(clk), .clr(reset));  // open: en
  Register #(.width(32)) _4 (.D(WD), .en(and_1_out), .Q(out__4), .clk(clk), .clr(reset));
  Register #(.width(32)) _8 (.D(WD), .en(and_2_out), .Q(out__8), .clk(clk), .clr(reset));
  Register #(.width(32)) _12 (.D(WD), .en(and_3_out), .Q(out__12), .clk(clk), .clr(reset));
  Register #(.width(32)) _16 (.D(WD), .en(and_4_out), .Q(out__16), .clk(clk), .clr(reset));
  Register #(.width(32)) _20 (.D(WD), .en(and_5_out), .Q(out__20), .clk(clk), .clr(reset));
  Register #(.width(32)) _24 (.D(WD), .en(and_6_out), .Q(out__24), .clk(clk), .clr(reset));
  Register #(.width(32)) _28 (.D(WD), .en(and_7_out), .Q(out__28), .clk(clk), .clr(reset));
  and and_8 (and_8_out, WE, data__1);
  and and_9 (and_9_out, WE, data__5);
  and and_10 (and_10_out, WE, data__9);
  and and_11 (and_11_out, WE, data__13);
  and and_12 (and_12_out, WE, data__17);
  and and_13 (and_13_out, WE, data__21);
  and and_14 (and_14_out, WE, data__25);
  and and_15 (and_15_out, WE, data__29);
  Register #(.width(32)) _1 (.D(WD), .en(and_8_out), .Q(out__1), .clk(clk), .clr(reset));
  Register #(.width(32)) _5 (.D(WD), .en(and_9_out), .Q(out__5), .clk(clk), .clr(reset));
  Register #(.width(32)) _9 (.D(WD), .en(and_10_out), .Q(out__9), .clk(clk), .clr(reset));
  Register #(.width(32)) _13 (.D(WD), .en(and_11_out), .Q(out__13), .clk(clk), .clr(reset));
  Register #(.width(32)) _17 (.D(WD), .en(and_12_out), .Q(out__17), .clk(clk), .clr(reset));
  Register #(.width(32)) _21 (.D(WD), .en(and_13_out), .Q(out__21), .clk(clk), .clr(reset));
  Register #(.width(32)) _25 (.D(WD), .en(and_14_out), .Q(out__25), .clk(clk), .clr(reset));
  Register #(.width(32)) _29 (.D(WD), .en(and_15_out), .Q(out__29), .clk(clk), .clr(reset));
  and and_16 (and_16_out, WE, data__2);
  and and_17 (and_17_out, WE, data__6);
  and and_18 (and_18_out, WE, data__10);
  and and_19 (and_19_out, WE, data__14);
  and and_20 (and_20_out, WE, data__18);
  and and_21 (and_21_out, WE, data__22);
  and and_22 (and_22_out, WE, data__26);
  and and_23 (and_23_out, WE, data__30);
  Register #(.width(32)) _2 (.D(WD), .en(and_16_out), .Q(out__2), .clk(clk), .clr(reset));
  Register #(.width(32)) _6 (.D(WD), .en(and_17_out), .Q(out__6), .clk(clk), .clr(reset));
  Register #(.width(32)) _10 (.D(WD), .en(and_18_out), .Q(out__10), .clk(clk), .clr(reset));
  Register #(.width(32)) _14 (.D(WD), .en(and_19_out), .Q(out__14), .clk(clk), .clr(reset));
  Register #(.width(32)) _18 (.D(WD), .en(and_20_out), .Q(out__18), .clk(clk), .clr(reset));
  Register #(.width(32)) _22 (.D(WD), .en(and_21_out), .Q(out__22), .clk(clk), .clr(reset));
  Register #(.width(32)) _26 (.D(WD), .en(and_22_out), .Q(out__26), .clk(clk), .clr(reset));
  Register #(.width(32)) _30 (.D(WD), .en(and_23_out), .Q(out__30), .clk(clk), .clr(reset));
  and and_24 (and_24_out, WE, data__3);
  and and_25 (and_25_out, WE, data__7);
  and and_26 (and_26_out, WE, data__11);
  and and_27 (and_27_out, WE, data__15);
  and and_28 (and_28_out, WE, data__19);
  and and_29 (and_29_out, WE, data__23);
  and and_30 (and_30_out, WE, data__27);
  and and_31 (and_31_out, WE, data__31);
  Multiplexer #(.select(5), .width(32)) multiplexer_1 (
    .in0(out__0), .in1(out__1), .in2(out__2), .in3(out__3), .in4(out__4), .in5(out__5), .in6(out__6),
    .in7(out__7), .in8(out__8), .in9(out__9), .in10(out__10), .in11(out__11), .in12(out__12), .in13(out__13),
    .in14(out__14), .in15(out__15), .in16(out__16), .in17(out__17), .in18(out__18), .in19(out__19),
    .in20(out__20), .in21(out__21), .in22(out__22), .in23(out__23), .in24(out__24), .in25(out__25),
    .in26(out__26), .in27(out__27), .in28(out__28), .in29(out__29), .in30(out__30), .in31(out__31),
    .out(RD1), .sel(A1));  // open: en
  Multiplexer #(.select(5), .width(32)) multiplexer_2 (
    .in0(out__0), .in1(out__1), .in2(out__2), .in3(out__3), .in4(out__4), .in5(out__5), .in6(out__6),
    .in7(out__7), .in8(out__8), .in9(out__9), .in10(out__10), .in11(out__11), .in12(out__12), .in13(out__13),
    .in14(out__14), .in15(out__15), .in16(out__16), .in17(out__17), .in18(out__18), .in19(out__19),
    .in20(out__20), .in21(out__21), .in22(out__22), .in23(out__23), .in24(out__24), .in25(out__25),
    .in26(out__26), .in27(out__27), .in28(out__28), .in29(out__29), .in30(out__30), .in31(out__31),
    .out(RD2), .sel(A2));  // open: en
  Register #(.width(32)) _3 (.D(WD), .en(and_24_out), .Q(out__3), .clk(clk), .clr(reset));
  Register #(.width(32)) _7 (.D(WD), .en(and_25_out), .Q(out__7), .clk(clk), .clr(reset));
  Register #(.width(32)) _11 (.D(WD), .en(and_26_out), .Q(out__11), .clk(clk), .clr(reset));
  Register #(.width(32)) _15 (.D(WD), .en(and_27_out), .Q(out__15), .clk(clk), .clr(reset));
  Register #(.width(32)) _19 (.D(WD), .en(and_28_out), .Q(out__19), .clk(clk), .clr(reset));
  Register #(.width(32)) _23 (.D(WD), .en(and_29_out), .Q(out__23), .clk(clk), .clr(reset));
  Register #(.width(32)) _27 (.D(WD), .en(and_30_out), .Q(out__27), .clk(clk), .clr(reset));
  Register #(.width(32)) _31 (.D(WD), .en(and_31_out), .Q(out__31), .clk(clk), .clr(reset));
endmodule

module ALU (
  input  [2:0] ALUCtrl__2_0,
  input  [31:0] A__31_0,
  input  [31:0] B__31_0,
  output Zero,
  output [31:0] Result
);

  wire subtractor_1_bout;
  wire [31:0] add, \and , \or , sub;

  assign \and  = A__31_0 & B__31_0;  // AND_Gate and_1, 32 bits wide
  assign \or  = A__31_0 | B__31_0;  // OR_Gate or_1, 32 bits wide
  Adder #(.width(32)) adder_1 (.a(A__31_0), .b(B__31_0), .out(add));  // open: cin, cout
  Subtractor #(.width(32)) subtractor_1 (.a(A__31_0), .b(B__31_0), .out(sub), .bout(subtractor_1_bout));  // open: bin
  Comparator #(.width(32)) comparator_1 (.a(A__31_0), .b(B__31_0), .eq(Zero));  // open: gt, lt
  Multiplexer #(.select(3), .width(32)) multiplexer_1 (
    .in0(\and ), .in1(\or ), .in2(add), .in6(sub), .out(Result), .sel(ALUCtrl__2_0));  // open: in3, in4, in5, in7, en

  // Other names for the same wires on the sheet: A[31:0] = A__31_0; B[31:0] = B__31_0
endmodule

module ALUCtrl (
  input  [2:0] ALUOp__2_0,
  input  [5:0] funct__5_0,
  output [2:0] ALUCtrl__2_0
);

  wire addu_out, beq_out, lui_out, lw_out, not_1_out, not_2_out, not_3_out, not_4_out, not_5_out, not_6_out,
       not_7_out, not_8_out, not_9_out, subu_out, sw_out;

  not not_1 (not_1_out, ALUOp__2_0[1]);
  not not_2 (not_2_out, ALUOp__2_0[2]);
  not not_3 (not_3_out, ALUOp__2_0[0]);
  not not_4 (not_4_out, funct__5_0[4]);
  not not_5 (not_5_out, funct__5_0[5]);
  not not_6 (not_6_out, funct__5_0[3]);
  not not_7 (not_7_out, funct__5_0[1]);
  not not_8 (not_8_out, funct__5_0[2]);
  not not_9 (not_9_out, funct__5_0[0]);
  and addu (addu_out, not_2_out, not_1_out, not_3_out, funct__5_0[5], not_4_out, not_6_out, not_8_out, not_7_out, funct__5_0[0]);
  and subu (subu_out, not_2_out, not_1_out, not_3_out, funct__5_0[5], not_4_out, not_6_out, not_8_out, funct__5_0[1], funct__5_0[0]);
  and ori (ALUCtrl__2_0[0], not_2_out, not_1_out, ALUOp__2_0[0]);
  and lw (lw_out, not_2_out, ALUOp__2_0[1], not_3_out);
  and sw (sw_out, not_2_out, ALUOp__2_0[1], not_3_out);
  and beq (beq_out, ALUOp__2_0[2], ALUOp__2_0[1], not_3_out);
  and lui (lui_out, not_2_out, ALUOp__2_0[1], ALUOp__2_0[0]);
  or ALUCtrl__2 (ALUCtrl__2_0[2], subu_out, beq_out);
  or ALUCtrl__1 (ALUCtrl__2_0[1], addu_out, subu_out, lw_out, sw_out, beq_out);
  // OR_Gate ALUCtrl__0 is placed but not wired
endmodule

module DM (
  input  [4:0] A__4_0,
  input  [31:0] WD__31_0,
  input  WE,
  input  Clk,
  input  RE,
  input  Reset,
  output [31:0] RD__31_0
);

  RAM #(.addrWidth(5), .dataWidth(32), .bus("separate")) ram_1 (
    .addr(A__4_0), .din(WD__31_0), .data(RD__31_0), .str(WE), .clk(Clk), .ld(RE), .clr(Reset));  // open: sel
endmodule

module EXT (
  input  [15:0] imm16__15_0,
  input  ExtOp,
  output [31:0] ext32__31_0
);

  wire [31:0] bit_extender_1_out, bit_extender_2_out;

  // Probe on bit_extender_1_out
  assign bit_extender_1_out = {{16{1'b0}}, imm16__15_0};  // Bit_Extender bit_extender_1
  assign bit_extender_2_out = {{16{imm16__15_0[15]}}, imm16__15_0};  // Bit_Extender bit_extender_2
  Multiplexer #(.width(32)) multiplexer_1 (
    .in0(bit_extender_1_out), .in1(bit_extender_2_out), .out(ext32__31_0), .sel(ExtOp));  // open: en
endmodule

module Ctrl (
  input  [5:0] opcode__5_0,
  input  [5:0] func__5_0,
  output NPCOp,
  output EXTOp,
  output RegWrite,
  output MemWrite,
  output M1_Sel,
  output M3_Sel,
  output [1:0] M2_Sel,
  output [2:0] ALUCtrl__2_0,
  output RE
);

  wire not_1_out, not_2_out, not_3_out, not_4_out, not_5_out, not_6_out, \R型指令_out ;
  wire [1:0] ori_out;

  not not_1 (not_1_out, opcode__5_0[5]);
  not not_2 (not_2_out, opcode__5_0[4]);
  not not_3 (not_3_out, opcode__5_0[3]);
  not not_4 (not_4_out, opcode__5_0[2]);
  not not_5 (not_5_out, opcode__5_0[1]);
  not not_6 (not_6_out, opcode__5_0[0]);
  and \R型指令  (\R型指令_out , not_1_out, not_2_out, not_3_out, not_4_out, not_5_out, not_6_out);
  and ori (ori_out[0], not_1_out, not_2_out, opcode__5_0[3], opcode__5_0[2], not_5_out, opcode__5_0[0]);
  and lw (M2_Sel[0], opcode__5_0[5], not_2_out, not_3_out, not_4_out, opcode__5_0[1], opcode__5_0[0]);
  and sw (MemWrite, opcode__5_0[5], not_2_out, opcode__5_0[3], not_4_out, opcode__5_0[1], opcode__5_0[0]);
  and beq (NPCOp, not_1_out, not_2_out, not_3_out, opcode__5_0[2], not_5_out, not_6_out);
  and lui (M2_Sel[1], not_1_out, not_2_out, opcode__5_0[3], opcode__5_0[2], opcode__5_0[1], opcode__5_0[0]);
  // OR_Gate NPCOp has open pins: in0=NPCOp, out=open
  // OR_Gate ALUOp__2 has open pins: in0=NPCOp, out=open
  // OR_Gate ALUOp__0 has open pins: in0=ori_out[0], out=open
  or ALUOp__1 (ori_out[1], M2_Sel[0], MemWrite, NPCOp);
  ALUCtrl aluctrl_1 (.ALUOp__2_0({NPCOp, ori_out}), .funct__5_0(func__5_0), .ALUCtrl__2_0(ALUCtrl__2_0));
  or u_EXTOp (EXTOp, M2_Sel[0], MemWrite);
  or u_RegWrite (RegWrite, \R型指令_out , ori_out[0], M2_Sel[0], M2_Sel[1]);
  // OR_Gate MemWrite has open pins: in0=MemWrite, out=open
  or u_M1_Sel (M1_Sel, ori_out[0], M2_Sel[0], M2_Sel[1]);
  // OR_Gate M2_Sel__1 has open pins: in0=M2_Sel[1], out=open
  // OR_Gate M2_Sel__0 has open pins: in0=M2_Sel[0], out=open
  or u_M3_Sel (M3_Sel, ori_out[0], M2_Sel[0], MemWrite);

  assign RE = M2_Sel[0];
endmodule

module test (
  input  [5:0] in_1,
  input  [5:0] in_2
);

  wire ctrl_1_p3, ctrl_1_p4, ctrl_1_p5, ctrl_1_p6, ctrl_1_p7, ctrl_1_p8, ctrl_1_p9, ctrl_1_p10;

  // Ctrl ctrl_1: pin names not known; wires that end beside it: in_1, in_2, ctrl_1_p3, ctrl_1_p4, ctrl_1_p5, ctrl_1_p6, ctrl_1_p7, ctrl_1_p8, ctrl_1_p9, ctrl_1_p10
  // Probe on ctrl_1_p3
  // Probe on ctrl_1_p10
  // Probe on ctrl_1_p4
  // Probe on ctrl_1_p5
  // Probe on ctrl_1_p6
  // Probe on ctrl_1_p7
  // Probe on ctrl_1_p8
  // Probe on ctrl_1_p9
endmodule

module SPL (
  input  [31:0] Instr,
  output [5:0] opcode____31_26,
  output [5:0] funct____5_0,
  output [4:0] rs____25_21,
  output [4:0] rt____20_16,
  output [4:0] rd____15_11,
  output [4:0] shamt____10_6
);


  assign funct____5_0 = Instr[5:0];
  assign opcode____31_26 = Instr[31:26];
  assign rd____15_11 = Instr[15:11];
  assign rs____25_21 = Instr[25:21];
  assign rt____20_16 = Instr[20:16];
  assign shamt____10_6 = Instr[10:6];

  // Other names for the same wires on the sheet: funct[5:0] = Instr[5:0]; opcode[5:0] = Instr[31:26];
  //   rd[4:0] = Instr[15:11]; rs[4:0] = Instr[25:21]; rt[4:0] = Instr[20:16]; shamt[4:0] = Instr[10:6]
endmodule

module get_address (
  input  [31:0] data,
  output [4:0] address
);


  assign address = data[6:2];
endmodule
