// Logisim project GRF_new.circ as structural Verilog
module grf_new (
  input  WE,
  input  clk,
  input  reset,
  input  [4:0] A1,
  input  [4:0] A2,
  input  [4:0] A3,
  input  [31:0] WD,
  output [31:0] RD1,
  output [31:0] RD2
);

  wire and_1_out, and_2_out, and_3_out, and_4_out, and_5_out, and_6_out, and_7_out, and_8_out, and_9_out,
       and_10_out, and_11_out, and_12_out, and_13_out, and_14_out, and_15_out, and_16_out, and_17_out,
       and_18_out, and_19_out, and_20_out, and_21_out, and_22_out, and_23_out, and_24_out, and_25_out,
       and_26_out, and_27_out, and_28_out, and_29_out, and_30_out, and_31_out, data__0, data__1, data__2,
       data__3, data__4, data__5, data__6, data__7, data__8, data__9, data__10, data__11, data__12, data__13,
       data__14, data__15, data__16, data__17, data__18, data__19, data__20, data__21, data__22, data__23,
       data__24, data__25, data__26, data__27, data__28, data__29, data__30, data__31;
  wire [31:0] out__0, out__1, out__2, out__3, out__4, out__5, out__6, out__7, out__8, out__9, out__10,
       out__11, out__12, out__13, out__14, out__15, out__16, out__17, out__18, out__19, out__20, out__21,
       out__22, out__23, out__24, out__25, out__26, out__27, out__28, out__29, out__30, out__31;

  and and_1 (and_1_out, WE, data__4);
  and and_2 (and_2_out, WE, data__8);
  and and_3 (and_3_out, WE, data__12);
  and and_4 (and_4_out, WE, data__16);
  and and_5 (and_5_out, WE, data__20);
  and and_6 (and_6_out, WE, data__24);
  and and_7 (and_7_out, WE, data__28);
  Decoder #(.select(5)) decoder_1 (
    .out0(data__0), .out1(data__1), .out2(data__2), .out3(data__3), .out4(data__4), .out5(data__5),
    .out6(data__6), .out7(data__7), .out8(data__8), .out9(data__9), .out10(data__10), .out11(data__11),
    .out12(data__12), .out13(data__13), .out14(data__14), .out15(data__15), .out16(data__16),
    .out17(data__17), .out18(data__18), .out19(data__19), .out20(data__20), .out21(data__21),
    .out22(data__22), .out23(data__23), .out24(data__24), .out25(data__25), .out26(data__26),
    .out27(data__27), .out28(data__28), .out29(data__29), .out30(data__30), .out31(data__31), .sel(A3));  // open: en
  Register #(.width(32)) _0 (.D({32{1'b0}}), .Q(out__0), .clk(clk), .clr(reset));  // open: en
  Register #(.width(32)) _4 (.D(WD), .en(and_1_out), .Q(out__4), .clk(clk), .clr(reset));
  Register #(.width(32)) _8 (.D(WD), .en(and_2_out), .Q(out__8), .clk(clk), .clr(reset));
  Register #(.width(32)) _12 (.D(WD), .en(and_3_out), .Q(out__12), .clk(clk), .clr(reset));
  Register #(.width(32)) _16 (.D(WD), .en(and_4_out), .Q(out__16), .clk(clk), .clr(reset));
  Register #(.width(32)) _20 (.D(WD), .en(and_5_out), .Q(out__20), .clk(clk), .clr(reset));
  Register #(.width(32)) _24 (.D(WD), .en(and_6_out), .Q(out__24), .clk(clk), .clr(reset));
  Register #(.width(32)) _28 (.D(WD), .en(and_7_out), .Q(out__28), .clk(clk), .clr(reset));
  and and_8 (and_8_out, WE, data__1);
  and and_9 (and_9_out, WE, data__5);
  and and_10 (and_10_out, WE, data__9);
  and and_11 (and_11_out, WE, data__13);
  and and_12 (and_12_out, WE, data__17);
  and and_13 (and_13_out, WE, data__21);
  and and_14 (and_14_out, WE, data__25);
  and and_15 (and_15_out, WE, data__29);
  Register #(.width(32)) _1 (.D(WD), .en(and_8_out), .Q(out__1), .clk(clk), .clr(reset));
  Register #(.width(32)) _5 (.D(WD), .en(and_9_out), .Q(out__5), .clk(clk), .clr(reset));
  Register #(.width(32)) _9 (.D(WD), .en(and_10_out), .Q(out__9), .clk(clk), .clr(reset));
  Register #(.width(32)) _13 (.D(WD), .en(and_11_out), .Q(out__13), .clk(clk), .clr(reset));
  Register #(.width(32)) _17 (.D(WD), .en(and_12_out), .Q(out__17), .clk(clk), .clr(reset));
  Register #(.width(32)) _21 (.D(WD), .en(and_13_out), .Q(out__21), .clk(clk), .clr(reset));
  Register #(.width(32)) _25 (.D(WD), .en(and_14_out), .Q(out__25), .clk(clk), .clr(reset));
  Register #(.width(32)) _29 (.D(WD), .en(and_15_out), .Q(out__29), .clk(clk), .clr(reset));
  and and_16 (and_16_out, WE, data__2);
  and and_17 (and_17_out, WE, data__6);
  and and_18 (and_18_out, WE, data__10);
  and and_19 (and_19_out, WE, data__14);
  and and_20 (and_20_out, WE, data__18);
  and and_21 (and_21_out, WE, data__22);
  and and_22 (and_22_out, WE, data__26);
  and and_23 (and_23_out, WE, data__30);
  Register #(.width(32)) _2 (.D(WD), .en(and_16_out), .Q(out__2), .clk(clk), .clr(reset));
  Register #(.width(32)) _6 (.D(WD), .en(and_17_out), .Q(out__6), .clk(clk), .clr(reset));
  Register #(.width(32)) _10 (.D(WD), .en(and_18_out), .Q(out__10), .clk(clk), .clr(reset));
  Register #(.width(32)) _14 (.D(WD), .en(and_19_out), .Q(out__14), .clk(clk), .clr(reset));
  Register #(.width(32)) _18 (.D(WD), .en(and_20_out), .Q(out__18), .clk(clk), .clr(reset));
  Register #(.width(32)) _22 (.D(WD), .en(and_21_out), .Q(out__22), .clk(clk), .clr(reset));
  Register #(.width(32)) _26 (.D(WD), .en(and_22_out), .Q(out__26), .clk(clk), .clr(reset));
  Register #(.width(32)) _30 (.D(WD), .en(and_23_out), .Q(out__30), .clk(clk), .clr(reset));
  and and_24 (and_24_out, WE, data__3);
  and and_25 (and_25_out, WE, data__7);
  and and_26 (and_26_out, WE, data__11);
  and and_27 (and_27_out, WE, data__15);
  and and_28 (and_28_out, WE, data__19);
  and and_29 (and_29_out, WE, data__23);
  and and_30 (and_30_out, WE, data__27);
  and and_31 (and_31_out, WE, data__31);
  Multiplexer #(.select(5), .width(32)) multiplexer_1 (
    .in0(out__0), .in1(out__1), .in2(out__2), .in3(out__3), .in4(out__4), .in5(out__5), .in6(out__6),
    .in7(out__7), .in8(out__8), .in9(out__9), .in10(out__10), .in11(out__11), .in12(out__12), .in13(out__13),
    .in14(out__14), .in15(out__15), .in16(out__16), .in17(out__17), .in18(out__18), .in19(out__19),
    .in20(out__20), .in21(out__21), .in22(out__22), .in23(out__23), .in24(out__24), .in25(out__25),
    .in26(out__26), .in27(out__27), .in28(out__28), .in29(out__29), .in30(out__30), .in31(out__31),
    .out(RD1), .sel(A1));  // open: en
  Multiplexer #(.select(5), .width(32)) multiplexer_2 (
    .in0(out__0), .in1(out__1), .in2(out__2), .in3(out__3), .in4(out__4), .in5(out__5), .in6(out__6),
    .in7(out__7), .in8(out__8), .in9(out__9), .in10(out__10), .in11(out__11), .in12(out__12), .in13(out__13),
    .in14(out__14), .in15(out__15), .in16(out__16), .in17(out__17), .in18(out__18), .in19(out__19),
    .in20(out__20), .in21(out__21), .in22(out__22), .in23(out__23), .in24(out__24), .in25(out__25),
    .in26(out__26), .in27(out__27), .in28(out__28), .in29(out__29), .in30(out__30), .in31(out__31),
    .out(RD2), .sel(A2));  // open: en
  Register #(.width(32)) _3 (.D(WD), .en(and_24_out), .Q(out__3), .clk(clk), .clr(reset));
  Register #(.width(32)) _7 (.D(WD), .en(and_25_out), .Q(out__7), .clk(clk), .clr(reset));
  Register #(.width(32)) _11 (.D(WD), .en(and_26_out), .Q(out__11), .clk(clk), .clr(reset));
  Register #(.width(32)) _15 (.D(WD), .en(and_27_out), .Q(out__15), .clk(clk), .clr(reset));
  Register #(.width(32)) _19 (.D(WD), .en(and_28_out), .Q(out__19), .clk(clk), .clr(reset));
  Register #(.width(32)) _23 (.D(WD), .en(and_29_out), .Q(out__23), .clk(clk), .clr(reset));
  Register #(.width(32)) _27 (.D(WD), .en(and_30_out), .Q(out__27), .clk(clk), .clr(reset));
  Register #(.width(32)) _31 (.D(WD), .en(and_31_out), .Q(out__31), .clk(clk), .clr(reset));
endmodule

module grf (
  input  clk,
  input  reset,
  input  WE,
  input  [4:0] A1,
  input  [4:0] A2,
  input  [4:0] A3,
  input  [31:0] WD,
  output [31:0] RD1,
  output [31:0] RD2
);

  wire and_1_out, and_2_out, and_3_out, and_4_out, and_5_out, and_6_out, and_7_out, and_8_out, and_9_out,
       and_10_out, and_11_out, and_12_out, and_13_out, and_14_out, and_15_out, and_16_out, and_17_out,
       and_18_out, and_19_out, and_20_out, and_21_out, and_22_out, and_23_out, and_24_out, and_25_out,
       and_26_out, and_27_out, and_28_out, and_29_out, and_30_out, and_31_out, data__0, data__1, data__2,
       data__3, data__4, data__5, data__6, data__7, data__8, data__9, data__10, data__11, data__12, data__13,
       data__14, data__15, data__16, data__17, data__18, data__19, data__20, data__21, data__22, data__23,
       data__24, data__25, data__26, data__27, data__28, data__29, data__30, data__31;
  wire [31:0] out__0, out__1, out__2, out__3, out__4, out__5, out__6, out__7, out__8, out__9, out__10,
       out__11, out__12, out__13, out__14, out__15, out__16, out__17, out__18, out__19, out__20, out__21,
       out__22, out__23, out__24, out__25, out__26, out__27, out__28, out__29, out__30, out__31;

  and and_1 (and_1_out, WE, data__4);
  and and_2 (and_2_out, WE, data__8);
  and and_3 (and_3_out, WE, data__12);
  and and_4 (and_4_out, WE, data__16);
  and and_5 (and_5_out, WE, data__20);
  and and_6 (and_6_out, WE, data__24);
  and and_7 (and_7_out, WE, data__28);
  Decoder #(.select(5)) decoder_1 (
    .out0(data__0), .out1(data__1), .out2(data__2), .out3(data__3), .out4(data__4), .out5(data__5),
    .out6(data__6), .out7(data__7), .out8(data__8), .out9(data__9), .out10(data__10), .out11(data__11),
    .out12(data__12), .out13(data__13), .out14(data__14), .out15(data__15), .out16(data__16),
    .out17(data__17), .out18(data__18), .out19(data__19), .out20(data__20), .out21(data__21),
    .out22(data__22), .out23(data__23), .out24(data__24), .out25(data__25), .out26(data__26),
    .out27(data__27), .out28(data__28), .out29(data__29), .out30(data__30), .out31(data__31), .sel(A3));  // open: en
  Register #(.width(32)) _0 (.D({32{1'b0}}), .Q(out__0), .clk(clk), .clr(reset));  // open: en
  Register #(.width(32)) _4 (.D(WD), .en(and_1_out), .Q(out__4), .clk(clk), .clr(reset));
  Register #(.width(32)) _8 (.D(WD), .en(and_2_out), .Q(out__8), .clk(clk), .clr(reset));
  Register #(.width(32)) _12 (.D(WD), .en(and_3_out), .Q(out__12), .clk(clk), .clr(reset));
  Register #(.width(32)) _16 (.D(WD), .en(and_4_out), .Q(out__16), .clk(clk), .clr(reset));
  Register #(.width(32)) _20 (.D(WD), .en(and_5_out), .Q(out__20), .clk(clk), .clr(reset));
  Register #(.width(32)) _24 (.D(WD), .en(and_6_out), .Q(out__24), .clk(clk), .clr(reset));
  Register #(.width(32)) _28 (.D(WD), .en(and_7_out), .Q(out__28), .clk(clk), .clr(reset));
  and and_8 (and_8_out, WE, data__1);
  and and_9 (and_9_out, WE, data__5);
  and and_10 (and_10_out, WE, data__9);
  and and_11 (and_11_out, WE, data__13);
  and and_12 (and_12_out, WE, data__17);
  and and_13 (and_13_out, WE, data__21);
  and and_14 (and_14_out, WE, data__25);
  and and_15 (and_15_out, WE, data__29);
  Register #(.width(32)) _1 (.D(WD), .en(and_8_out), .Q(out__1), .clk(clk), .clr(reset));
  Register #(.width(32)) _5 (.D(WD), .en(and_9_out), .Q(out__5), .clk(clk), .clr(reset));
  Register #(.width(32)) _9 (.D(WD), .en(and_10_out), .Q(out__9), .clk(clk), .clr(reset));
  Register #(.width(32)) _13 (.D(WD), .en(and_11_out), .Q(out__13), .clk(clk), .clr(reset));
  Register #(.width(32)) _17 (.D(WD), .en(and_12_out), .Q(out__17), .clk(clk), .clr(reset));
  Register #(.width(32)) _21 (.D(WD), .en(and_13_out), .Q(out__21), .clk(clk), .clr(reset));
  Register #(.width(32)) _25 (.D(WD), .en(and_14_out), .Q(out__25), .clk(clk), .clr(reset));
  Register #(.width(32)) _29 (.D(WD), .en(and_15_out), .Q(out__29), .clk(clk), .clr(reset));
  and and_16 (and_16_out, WE, data__2);
  and and_17 (and_17_out, WE, data__6);
  and and_18 (and_18_out, WE, data__10);
  and and_19 (and_19_out, WE, data__14);
  and and_20 (and_20_out, WE, data__18);
  and and_21 (and_21_out, WE, data__22);
  and and_22 (and_22_out, WE, data__26);
  and and_23 (and_23_out, WE, data__30);
  Register #(.width(32)) _2 (.D(WD), .en(and_16_out), .Q(out__2), .clk(clk), .clr(reset));
  Register #(.width(32)) _6 (.D(WD), .en(and_17_out), .Q(out__6), .clk(clk), .clr(reset));
  Register #(.width(32)) _10 (.D(WD), .en(and_18_out), .Q(out__10), .clk(clk), .clr(reset));
  Register #(.width(32)) _14 (.D(WD), .en(and_19_out), .Q(out__14), .clk(clk), .clr(reset));
  Register #(.width(32)) _18 (.D(WD), .en(and_20_out), .Q(out__18), .clk(clk), .clr(reset));
  Register #(.width(32)) _22 (.D(WD), .en(and_21_out), .Q(out__22), .clk(clk), .clr(reset));
  Register #(.width(32)) _26 (.D(WD), .en(and_22_out), .Q(out__26), .clk(clk), .clr(reset));
  Register #(.width(32)) _30 (.D(WD), .en(and_23_out), .Q(out__30), .clk(clk), .clr(reset));
  and and_24 (and_24_out, WE, data__3);
  and and_25 (and_25_out, WE, data__7);
  and and_26 (and_26_out, WE, data__11);
  and and_27 (and_27_out, WE, data__15);
  and and_28 (and_28_out, WE, data__19);
  and and_29 (and_29_out, WE, data__23);
  and and_30 (and_30_out, WE, data__27);
  and and_31 (and_31_out, WE, data__31);
  Multiplexer #(.select(5), .width(32)) multiplexer_1 (
    .in0(out__0), .in1(out__1), .in2(out__2), .in3(out__3), .in4(out__4), .in5(out__5), .in6(out__6),
    .in7(out__7), .in8(out__8), .in9(out__9), .in10(out__10), .in11(out__11), .in12(out__12), .in13(out__13),
    .in14(out__14), .in15(out__15), .in16(out__16), .in17(out__17), .in18(out__18), .in19(out__19),
    .in20(out__20), .in21(out__21), .in22(out__22), .in23(out__23), .in24(out__24), .in25(out__25),
    .in26(out__26), .in27(out__27), .in28(out__28), .in29(out__29), .in30(out__30), .in31(out__31),
    .out(RD1), .sel(A1));  // open: en
  Multiplexer #(.select(5), .width(32)) multiplexer_2 (
    .in0(out__0), .in1(out__1), .in2(out__2), .in3(out__3), .in4(out__4), .in5(out__5), .in6(out__6),
    .in7(out__7), .in8(out__8), .in9(out__9), .in10(out__10), .in11(out__11), .in12(out__12), .in13(out__13),
    .in14(out__14), .in15(out__15), .in16(out__16), .in17(out__17), .in18(out__18), .in19(out__19),
    .in20(out__20), .in21(out__21), .in22(out__22), .in23(out__23), .in24(out__24), .in25(out__25),
    .in26(out__26), .in27(out__27), .in28(out__28), .in29(out__29), .in30(out__30), .in31(out__31),
    .out(RD2), .sel(A2));  // open: en
  Register #(.width(32)) _3 (.D(WD), .en(and_24_out), .Q(out__3), .clk(clk), .clr(reset));
  Register #(.width(32)) _7 (.D(WD), .en(and_25_out), .Q(out__7), .clk(clk), .clr(reset));
  Register #(.width(32)) _11 (.D(WD), .en(and_26_out), .Q(out__11), .clk(clk), .clr(reset));
  Register #(.width(32)) _15 (.D(WD), .en(and_27_out), .Q(out__15), .clk(clk), .clr(reset));
  Register #(.width(32)) _19 (.D(WD), .en(and_28_out), .Q(out__19), .clk(clk), .clr(reset));
  Register #(.width(32)) _23 (.D(WD), .en(and_29_out), .Q(out__23), .clk(clk), .clr(reset));
  Register #(.width(32)) _27 (.D(WD), .en(and_30_out), .Q(out__27), .clk(clk), .clr(reset));
  Register #(.width(32)) _31 (.D(WD), .en(and_31_out), .Q(out__31), .clk(clk), .clr(reset));
endmodule
